# Fritzing sketch esp32+level-converter (saved by Fritzing 0.9.2b)
circuit board: 7cm x 5cm
breadboards: 2

parts:
  Part2 = Logic Level Converter
  Part1 = Logic Level Converter
  U1 = ESP32-38PinWide [part_number=ESP32-38PinWide]
  J1 = LOAD_CELL [package=1x03]  # not connected
  J2 = LOAD_CELL [package=1x03]  # not connected
  J3 = LOAD_CELL [package=1x03]  # not connected
  J4 = LOAD_CELL [package=1x03]  # not connected
  R1 = Resistor [tolerance=±5% resistance=220 package=THT]
  LED1 = LED - 3mm [color="Red (633nm)" package="3 mm [THT]"]

nets:
  N1: Part2.TX2_LV, U1.GPIO19
  N2: Part2.RX2_LV, U1.GPIO18
  N3: Part2.LV, Part2.HV, Part1.LV, Part1.HV, U1.3.3, U1.VIN
  N4: Part2.GND, LED1.anode
  N5: Part2.RX_LV, U1.GPIO17
  N6: Part2.TX_LV, U1.GPIO16
  N7: Part1.TX2_LV, U1.GPIO32
  N8: Part1.RX2_LV, U1.GPIO33
  N9: Part1.GND#3, U1.GND
  N10: Part1.RX_LV, U1.GPIO26
  N11: Part1.TX_LV, U1.GPIO27
  N12: U1.GPIO5, R1.Pin_1
  N13: R1.Pin_0, LED1.cathode

custom parts:
  Logic Level Converter: Description: If you've ever tried to connect a 3.3V device to a 5V system, you know what a challenge it can be. The SparkFun logic level converter is a small device that safely steps down 5V signals to 3.3V and steps up 3.3V to 5V. This level converter also works with 2.8V and 1.8V devices. Each level converter has the capability of converting 4 pins on the high side to 4 pins on the low side.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
  ESP32-38PinWide: Generic 38-Pin ESP32 with wide format (only access to one side of pins on a breadboard) based on Stephen Lilley's HiLetgo ESP-WROOM-32 ESP32 ESP-32S Development Board.
